# Fritzing sketch eink_weather_clock (saved by Fritzing 0.9.9b)

parts:
  A1 = Waveshare 1.54in epaper display
  U1 = ESP32-38PinWide [part_number=ESP32-38PinWide]

nets:
  N1: A1.Pin_1, U1.GPIO12
  N2: A1.Pin_2, U1.GPIO26
  N3: A1.Pin_3, U1.GPIO27
  N4: A1.Pin_4, U1.GPIO16
  N5: A1.Pin_5, U1.GPIO17
  N6: A1.Pin_6, U1.GPIO33
  N7: A1.Pin_7, U1.GND
  N8: A1.Pin_8, U1.3.3

custom parts:
  Waveshare 1.54in epaper display: This is an E-Ink display module, 1.54inch, 200x200 resolution, with embedded controller, communicating via SPI interface.
  ESP32-38PinWide: Generic 38-Pin ESP32 with wide format (only access to one side of pins on a breadboard) based on Stephen Lilley's HiLetgo ESP-WROOM-32 ESP32 ESP-32S Development Board.
